// Logisim project dividerByStar.circ as structural Verilog
module counter (
  input  in_1,
  output out_2,
  output out_3,
  output out_4,
  output out_5,
  output out_6,
  output out_7,
  output out_8,
  output out_9
);

  wire and_1_out, and_2_out, and_3_out, and_4_out, and_5_out, and_6_out;

  J_K_Flip_Flop j_k_ff_1 (.J(1'b1), .clk(in_1), .K(1'b1), .Q(out_2));  // open: Qn, preset, en, reset
  J_K_Flip_Flop j_k_ff_2 (.J(out_2), .clk(in_1), .K(out_2), .Q(out_3));  // open: Qn, preset, en, reset
  and and_1 (and_1_out, out_3, out_2);
  J_K_Flip_Flop j_k_ff_3 (.J(and_1_out), .clk(in_1), .K(and_1_out), .Q(out_4));  // open: Qn, preset, en, reset
  and and_2 (and_2_out, out_2, out_3, out_4);
  J_K_Flip_Flop j_k_ff_4 (.J(and_2_out), .clk(in_1), .K(and_2_out), .Q(out_5));  // open: Qn, preset, en, reset
  and and_3 (and_3_out, out_2, out_3, out_4, out_5);
  J_K_Flip_Flop j_k_ff_5 (.J(and_3_out), .clk(in_1), .K(and_3_out), .Q(out_6));  // open: Qn, preset, en, reset
  J_K_Flip_Flop j_k_ff_6 (.J(and_4_out), .clk(in_1), .K(and_4_out), .Q(out_7));  // open: Qn, preset, en, reset
  and and_4 (and_4_out, out_2, out_3, out_4, out_5, out_6);
  and and_5 (and_5_out, out_2, out_3, out_4, out_5, out_6, out_7);
  J_K_Flip_Flop j_k_ff_7 (.J(and_5_out), .clk(in_1), .K(and_5_out), .Q(out_8));  // open: Qn, preset, en, reset
  and and_6 (and_6_out, out_8, out_2, out_3, out_4, out_5, out_6, out_7);
  J_K_Flip_Flop j_k_ff_8 (.J(and_6_out), .clk(in_1), .K(and_6_out), .Q(out_9));  // open: Qn, preset, en, reset
endmodule
