// Logisim project Controlador.circ as structural Verilog: 1 circuit, main circuit main
// 8
module main (
  input  in_1,
  input  in_2,
  input  in_3,
  input  in_4,
  input  in_5,
  input  in_6,
  input  [7:0] PC,
  input  in_8,
  input  in_9,
  input  PEGA_PC,
  input  PEGA_IR,
  input  PEGA_IR_2
);

  wire multiplexer_1_p2, not_1_out, or_1_out;
  wire [7:0] \Endereço , \Instrução , IREnd;
  wire [15:0] AEnd, demultiplexer_1_out1, IrIN, transistor_1_out, Valor;

  // Probe on IrIN
  Register #(.width(16)) register_1 (.D(IrIN), .en(in_3), .Q({IREnd, \Instrução }), .clk(in_4), .clr(in_5));
  // Multiplexer #(.select(2), .enable("false")) multiplexer_1: pin names not known; wires that end beside it: \Endereço , multiplexer_1_p2
  or or_1 (or_1_out, PEGA_PC, PEGA_IR);
  and and_1 (multiplexer_1_p2, PEGA_IR, not_1_out);
  not not_1 (not_1_out, PEGA_PC);
  // Probe on \Endereço 
  Demultiplexer #(.width(16)) demultiplexer_1 (
    .out0(IrIN), .out1(demultiplexer_1_out1), .in(transistor_1_out), .sel(multiplexer_1_p2), .en(or_1_out));
  Transistor #(.\type ("n"), .width(16)) transistor_1 (.in(Valor), .out(transistor_1_out), .gate(or_1_out));
  Transistor #(.\type ("n"), .width(16)) transistor_2 (.in(AEnd), .out(Valor), .gate(PEGA_IR_2));
  // Probe on Valor
  // Probe on demultiplexer_1_out1
  RAM #(.dataWidth(16)) ram_1 (.addr(\Endereço ), .data(Valor), .sel(1'b1), .clk(in_1), .ld(in_6), .clr(in_2));
  Register #(.width(16)) register_2 (.D(demultiplexer_1_out1), .en(1'b1), .Q(AEnd), .clk(in_8), .clr(in_9));
  // Probe on Valor

  // Other names for the same wires on the sheet: STA = PEGA_IR_2
endmodule
